# Fritzing sketch LW3_Sketch (saved by Fritzing 0.9.3b)

parts:
  Bauteil1 = Arduino Mega 2560 (Rev3)
  RGB_SMD_LED1 = SMD RGB LED (WS2812) [package=5050]
  LED1 = smd LED [color="Red (633nm)" package="0805 [SMD]"]
  R1 = Resistor [tolerance=±5% resistance=220 package="0603 [SMD]"]
  RGB_SMD_LED2 = SMD RGB LED (WS2812) [package=5050]
  RGB_GI = SMD RGB LED (WS2812) [package=5050]
  GND = female pin header, 2 pins [form="♀ (female)"]
  CN10 = female pin header, 2 pins [form="♀ (female)"]
  J5 = female pin header, 2 pins [form="♀ (female)"]
  J6 = female pin header, 2 pins [form="♀ (female)"]
  J9 = female pin header, 2 pins [form="♀ (female)"]  # not connected
  J10 = female pin header, 2 pins [form="♀ (female)"]  # not connected
  CN8 = female pin header, 2 pins [form="♀ (female)"]
  RGB_FLFI_Left = SMD RGB LED (WS2812) [package=5050]
  RGB_FLIFI_Right = SMD RGB LED (WS2812) [package=5050]
  J11 = Dagu DGServo 9g header connector (female) [package=THT]  # not connected
  J12 = Dagu DGServo 9g header connector (female) [package=THT]
  Key = Dagu DGServo 9g header (male) [package=THT]  # not connected
  Key_2 = Dagu DGServo 9g header (male) [package=THT]
  Switching_Power_Supply_5V_/_6A = Screw terminal - 2 pins [package=THT]

nets:
  VSS: Bauteil1.GND, RGB_SMD_LED1.VSS, R1.Pin_1, RGB_SMD_LED2.VSS, RGB_GI.VSS, GND.pin2, RGB_FLFI_Left.VSS, RGB_FLIFI_Right.VSS, Switching_Power_Supply_5V_/_6A.pin1
  N1: Bauteil1.D13_PWM, LED1.anode
  N2: Bauteil1.D12_PWM, RGB_SMD_LED1.DIn
  N3: Bauteil1.D11_PWM, RGB_FLFI_Left.DIn
  N4: Bauteil1.D10_PWM, RGB_FLIFI_Right.DIn
  VDD: Bauteil1.5V, RGB_SMD_LED1.VDD, RGB_SMD_LED2.VDD, RGB_GI.VDD, RGB_FLFI_Left.VDD, RGB_FLIFI_Right.VDD, Switching_Power_Supply_5V_/_6A.pin2
  N5: Bauteil1.D2_PWM, CN8.pin2
  N6: Bauteil1.D22, J6.pin1
  N7: Bauteil1.D23, J6.pin2
  N8: Bauteil1.D24, J5.pin2
  N9: Bauteil1.D25, CN10.pin1
  N10: Bauteil1.D26, CN10.pin2, Key_2.gnd
  N11: Bauteil1.D27, J12.gnd, Key_2.pulse
  N12: Bauteil1.D28, J12.Vcc
  N13: Bauteil1.D29, J12.pulse
  N14: RGB_SMD_LED1.DOut, RGB_SMD_LED2.DIn
  N15: LED1.cathode, R1.Pin_0
  N16: RGB_SMD_LED2.DOut, RGB_GI.DIn

notes:
  GI: 36 LEDs
  FLIFI Left: 4 LEDs
  FLIFI Right: 4 LEDs
